# Fritzing sketch Robot Orchestra stage 3 (saved by Fritzing 0.9.3b)
breadboards: 1

parts:
  Part1 = Arduino Uno (Rev3) - ICSP
  LED1 = smd LED [color="Green (555nm)" package="0805 [SMD]"]

nets:
  N1: Part1.D3_PWM, LED1.anode
  N2: Part1.GND, LED1.cathode
