# Fritzing sketch Robot Orchestra stage 4 (saved by Fritzing 0.9.3b)
breadboards: 1

parts:
  Part1 = Arduino Uno (Rev3) - ICSP
  LED1 = smd LED [color="Green (555nm)" package="0805 [SMD]"]
  J1 = Basic Servo

nets:
  N1: Part1.D9_PWM, J1.pulse
  N2: Part1.D3_PWM, LED1.anode
  5V: Part1.5V, J1.vcc
  GND: Part1.GND, LED1.cathode, J1.gnd
