# Fritzing sketch Huzzah Robot Diagram (saved by Fritzing 0.9.3b)
breadboards: 1

parts:
  Adafruit_HUZZAH_ESP8266_Breakout1 = Adafruit HUZZAH ESP8266 Breakout [part_number=2471]
  J1 = Basic Servo
  VCC1 = 4 x AAA Battery Mount

nets:
  GND: Adafruit_HUZZAH_ESP8266_Breakout1.GND, J1.gnd, VCC1.-
  N1: Adafruit_HUZZAH_ESP8266_Breakout1.VBat, J1.vcc, VCC1.+
  N2: Adafruit_HUZZAH_ESP8266_Breakout1.#12, J1.pulse
